// Logisim project 21CPU.circ as structural Verilog: 10 circuits, main circuit main
module main (
  input  in_1,
  output [31:0] out_2,
  output out_3,
  output [4:0] out_4,
  output [31:0] out_5,
  output out_6,
  output [4:0] out_7,
  output [31:0] out_8
);

  wire ALUDataSrc, branch, clk, EXTOp, MemDataSrc;
  wire [1:0] RegAddrSrc, RegDataSrc;
  wire [2:0] NPCOp;
  wire [3:0] ALUControl;
  wire [4:0] instr_plexer_1_out_4, instr_plexer_1_out_5, instr_plexer_1_out_6, shamt;
  wire [5:0] instr_plexer_1_out_2, instr_plexer_1_out_3;
  wire [15:0] instr_plexer_1_out_8;
  wire [31:0] ALUResult, dm_1_out_6, ext_1_out_3, grf_1_rd1, multiplexer_2_out, PC_4, RD2;

  IFU ifu_1 (
    .branch(branch), .NPCOp(NPCOp), .out_6(out_2), .clk(clk), .reset(in_1), .out_7(PC_4),
    .in_4({ALUResult[31:7], out_7, ALUResult[1:0]}));
  Clock clock_1 (.out(clk));
  instr_Plexer instr_plexer_1 (
    .in_1(out_2), .out_2(instr_plexer_1_out_2), .out_4(instr_plexer_1_out_4), .out_5(instr_plexer_1_out_5),
    .out_6(instr_plexer_1_out_6), .out_7(shamt), .out_8(instr_plexer_1_out_8), .out_3(instr_plexer_1_out_3));
  EXT ext_1 (.in_2(instr_plexer_1_out_8), .out_3(ext_1_out_3), .EXTOp(EXTOp));
  CU cu_1 (
    .opcode(instr_plexer_1_out_2), .func(instr_plexer_1_out_3), .out_9(RegDataSrc), .out_3(out_6),
    .out_5(ALUDataSrc), .out_11(ALUControl), .out_8(RegAddrSrc), .out_6(out_3), .out_4(EXTOp),
    .out_10(NPCOp), .out_7(MemDataSrc));
  GRF grf_1 (
    .A1(instr_plexer_1_out_4), .A2(instr_plexer_1_out_5), .A3(out_4), .WD3(out_5), .RD1(grf_1_rd1),
    .RD2(RD2), .clk(clk), .reset(in_1), .WE3(out_3));
  Multiplexer #(.select(2), .width(5), .enable("false")) multiplexer_1 (
    .in0(instr_plexer_1_out_5), .in1(instr_plexer_1_out_6), .in2({5{1'b1}}), .out(out_4), .sel(RegAddrSrc));  // open: in3
  Multiplexer #(.width(32), .enable("false")) multiplexer_2 (
    .in0(RD2), .in1(ext_1_out_3), .out(multiplexer_2_out), .sel(ALUDataSrc));
  ALU alu_1 (
    .A(grf_1_rd1), .B(multiplexer_2_out), .out_5(branch), .out_6({ALUResult[31:7], out_7, ALUResult[1:0]}),
    .ALUControl(ALUControl), .in_4(shamt));
  Multiplexer #(.width(32), .enable("false")) multiplexer_3 (.in0(RD2), .out(out_8), .sel(MemDataSrc));  // open: in1
  DM dm_1 (
    .A({ALUResult[31:7], out_7, ALUResult[1:0]}), .WD(out_8), .out_6(dm_1_out_6), .in_1(clk), .in_2(out_6),
    .in_5(in_1));
  Multiplexer #(.select(2), .width(32), .enable("false")) multiplexer_4 (
    .in0({ALUResult[31:7], out_7, ALUResult[1:0]}), .in1(dm_1_out_6), .in2(PC_4), .out(out_5),
    .sel(RegDataSrc));  // open: in3

  // Other names for the same wires on the sheet: ALUResult[6:2] = out_7; MemAddr[4:0] = out_7; instr[31:0] = out_2;
  //   MemData[31:0] = out_8; MemWrite = out_6; RegAddr[4:0] = out_4; RegData[31:0] = out_5; RegWrite = out_3;
  //   reset = in_1
endmodule

module IFU (
  input  clk,
  input  branch,
  input  [2:0] NPCOp,
  input  [31:0] in_4,
  input  reset,
  output [31:0] out_6,
  output [31:0] out_7
);

  wire [31:0] npc_1_out_6, PC;

  NPC npc_1 (.branch(branch), .NPCOp(NPCOp), .instr(out_6), .PC(PC), .out_6(npc_1_out_6), .ALUResult(in_4));
  Register #(.width(32)) u_PC (.D(npc_1_out_6), .Q(PC), .clk(clk), .clr(reset));  // open: en
  Adder #(.width(32)) adder_1 (.a(PC), .b(32'h4), .out(out_7));  // open: cin, cout
  ROM #(.addrWidth(10), .dataWidth(32)) rom_1 (.addr(PC[11:2]), .data(out_6));  // open: sel

  // Other names for the same wires on the sheet: ALUResult[31:0] = in_4; instr[31:0] = out_6; PC_4[31:0] = out_7

  // Notes on the sheet:
  //   contents of rom_1 (hex, n*v repeats v):
  //   340a300c 8000c09 3c010000 34210001 1615821 3c010000 3421abcd 1e17820 1200008 3c010000 3421abcd
  //   1e17820 1404809 18f7024 1404809 1404809 1404809 8000c16 3c010000 34210063 1a16821 3e00008 c000c12
  //   8000c00
endmodule

module NPC (
  input  branch,
  input  [2:0] NPCOp,
  input  [31:0] instr,
  input  [31:0] PC,
  input  [31:0] ALUResult,
  output [31:0] out_6
);

  wire [31:0] adder_2_out, bit_extender_1_out, multiplexer_2_out, PC_4, PC_4_sign_extend_imm16__00,
       shifter_1_out;

  assign bit_extender_1_out = {{16{instr[15]}}, instr[15:0]};  // Bit_Extender bit_extender_1
  Shifter #(.width(32)) shifter_1 (.in(bit_extender_1_out), .\dist (5'b00010), .out(shifter_1_out));
  Adder #(.width(32)) adder_1 (.a(PC), .b(32'h4), .out(PC_4));  // open: cin, cout
  Adder #(.width(32)) adder_2 (.a(PC_4), .b(shifter_1_out), .out(adder_2_out));  // open: cin, cout
  Multiplexer #(.width(32), .enable("false")) multiplexer_1 (
    .in0(PC_4), .in1(adder_2_out), .out(PC_4_sign_extend_imm16__00), .sel(branch));
  Multiplexer #(.select(3), .width(32), .enable("false")) multiplexer_2 (
    .in0(PC_4), .in1(PC_4_sign_extend_imm16__00), .in2({PC[31:28], instr[25:0], 2'b00}), .in4(ALUResult),
    .out(multiplexer_2_out), .sel(NPCOp));  // open: in3, in5, in6, in7
  assign out_6 = 32'hfff & multiplexer_2_out;  // AND_Gate and_1, 32 bits wide

  // Other names for the same wires on the sheet: GRF_rs[31:0] = ALUResult; NPC[31:0] = out_6;
  //   PC31__28__imm26__00[31:2] = {PC[31:28], instr[25:0]}

  // Notes on the sheet:
  //   NPCOp: 00 for R-instr           01 for branch              10 for J-instr
endmodule

module instr_Plexer (
  input  [31:0] in_1,
  output [5:0] out_2,
  output [5:0] out_3,
  output [4:0] out_4,
  output [4:0] out_5,
  output [4:0] out_6,
  output [4:0] out_7,
  output [15:0] out_8
);


  assign out_2 = in_1[31:26];
  assign out_3 = in_1[5:0];
  assign out_4 = in_1[25:21];
  assign out_5 = in_1[20:16];
  assign out_6 = in_1[15:11];
  assign out_7 = in_1[10:6];
  assign out_8 = in_1[15:0];
endmodule

module GRF (
  input  [4:0] A1,
  input  clk,
  input  reset,
  input  WE3,
  input  [4:0] A2,
  input  [4:0] A3,
  input  [31:0] WD3,
  output [31:0] RD1,
  output [31:0] RD2
);

  wire demultiplexer_1_out1, demultiplexer_1_out2, demultiplexer_1_out3, demultiplexer_1_out4,
       demultiplexer_1_out5, demultiplexer_1_out6, demultiplexer_1_out7, demultiplexer_1_out8,
       demultiplexer_1_out9, demultiplexer_1_out10, demultiplexer_1_out11, demultiplexer_1_out12,
       demultiplexer_1_out13, demultiplexer_1_out14, demultiplexer_1_out15, demultiplexer_1_out16,
       demultiplexer_1_out17, demultiplexer_1_out18, demultiplexer_1_out19, demultiplexer_1_out20,
       demultiplexer_1_out21, demultiplexer_1_out22, demultiplexer_1_out23, demultiplexer_1_out24,
       demultiplexer_1_out25, demultiplexer_1_out26, demultiplexer_1_out27, demultiplexer_1_out28,
       demultiplexer_1_out29, demultiplexer_1_out30, demultiplexer_1_out31;
  wire [31:0] _0, _1, _2, _3, _4, _5, _6, _7, _8, _9, _10, _11, _12, _13, _14, _15, _16, _17, _18, _19, _20,
       _21, _22, _23, _24, _25, _26, _27, _28, _29, _30, _31;

  Demultiplexer #(.select(5), .disabled(0), .enable("false")) demultiplexer_1 (
    .out1(demultiplexer_1_out1), .out2(demultiplexer_1_out2), .out3(demultiplexer_1_out3),
    .out4(demultiplexer_1_out4), .out5(demultiplexer_1_out5), .out6(demultiplexer_1_out6),
    .out7(demultiplexer_1_out7), .out8(demultiplexer_1_out8), .out9(demultiplexer_1_out9),
    .out10(demultiplexer_1_out10), .out11(demultiplexer_1_out11), .out12(demultiplexer_1_out12),
    .out13(demultiplexer_1_out13), .out14(demultiplexer_1_out14), .out15(demultiplexer_1_out15),
    .out16(demultiplexer_1_out16), .out17(demultiplexer_1_out17), .out18(demultiplexer_1_out18),
    .out19(demultiplexer_1_out19), .out20(demultiplexer_1_out20), .out21(demultiplexer_1_out21),
    .out22(demultiplexer_1_out22), .out23(demultiplexer_1_out23), .out24(demultiplexer_1_out24),
    .out25(demultiplexer_1_out25), .out26(demultiplexer_1_out26), .out27(demultiplexer_1_out27),
    .out28(demultiplexer_1_out28), .out29(demultiplexer_1_out29), .out30(demultiplexer_1_out30),
    .out31(demultiplexer_1_out31), .in(WE3), .sel(A3));  // open: out0
  Register #(.width(32)) register_1 (.Q(_0));  // open: D, en, clk, clr
  Register #(.width(32)) register_2 (.D(WD3), .en(demultiplexer_1_out1), .Q(_1), .clk(clk), .clr(reset));
  Register #(.width(32)) register_3 (.D(WD3), .en(demultiplexer_1_out2), .Q(_2), .clk(clk), .clr(reset));
  Register #(.width(32)) register_4 (.D(WD3), .en(demultiplexer_1_out3), .Q(_3), .clk(clk), .clr(reset));
  Register #(.width(32)) register_5 (.D(WD3), .en(demultiplexer_1_out4), .Q(_4), .clk(clk), .clr(reset));
  Register #(.width(32)) register_6 (.D(WD3), .en(demultiplexer_1_out5), .Q(_5), .clk(clk), .clr(reset));
  Register #(.width(32)) register_7 (.D(WD3), .en(demultiplexer_1_out6), .Q(_6), .clk(clk), .clr(reset));
  Register #(.width(32)) register_8 (.D(WD3), .en(demultiplexer_1_out7), .Q(_7), .clk(clk), .clr(reset));
  Register #(.width(32)) register_9 (.D(WD3), .en(demultiplexer_1_out8), .Q(_8), .clk(clk), .clr(reset));
  Register #(.width(32)) register_10 (.D(WD3), .en(demultiplexer_1_out9), .Q(_9), .clk(clk), .clr(reset));
  Register #(.width(32)) register_11 (.D(WD3), .en(demultiplexer_1_out10), .Q(_10), .clk(clk), .clr(reset));
  Register #(.width(32)) register_12 (.D(WD3), .en(demultiplexer_1_out11), .Q(_11), .clk(clk), .clr(reset));
  Register #(.width(32)) register_13 (.D(WD3), .en(demultiplexer_1_out12), .Q(_12), .clk(clk), .clr(reset));
  Register #(.width(32)) register_14 (.D(WD3), .en(demultiplexer_1_out13), .Q(_13), .clk(clk), .clr(reset));
  Register #(.width(32)) register_15 (.D(WD3), .en(demultiplexer_1_out14), .Q(_14), .clk(clk), .clr(reset));
  Register #(.width(32)) register_16 (.D(WD3), .en(demultiplexer_1_out15), .Q(_15), .clk(clk), .clr(reset));
  Register #(.width(32)) register_17 (.D(WD3), .en(demultiplexer_1_out16), .Q(_16), .clk(clk), .clr(reset));
  Register #(.width(32)) register_18 (.D(WD3), .en(demultiplexer_1_out17), .Q(_17), .clk(clk), .clr(reset));
  Register #(.width(32)) register_19 (.D(WD3), .en(demultiplexer_1_out18), .Q(_18), .clk(clk), .clr(reset));
  Register #(.width(32)) register_20 (.D(WD3), .en(demultiplexer_1_out19), .Q(_19), .clk(clk), .clr(reset));
  Register #(.width(32)) register_21 (.D(WD3), .en(demultiplexer_1_out20), .Q(_20), .clk(clk), .clr(reset));
  Register #(.width(32)) register_22 (.D(WD3), .en(demultiplexer_1_out21), .Q(_21), .clk(clk), .clr(reset));
  Register #(.width(32)) register_23 (.D(WD3), .en(demultiplexer_1_out22), .Q(_22), .clk(clk), .clr(reset));
  Register #(.width(32)) register_24 (.D(WD3), .en(demultiplexer_1_out23), .Q(_23), .clk(clk), .clr(reset));
  Register #(.width(32)) register_25 (.D(WD3), .en(demultiplexer_1_out24), .Q(_24), .clk(clk), .clr(reset));
  Register #(.width(32)) register_26 (.D(WD3), .en(demultiplexer_1_out25), .Q(_25), .clk(clk), .clr(reset));
  Register #(.width(32)) register_27 (.D(WD3), .en(demultiplexer_1_out26), .Q(_26), .clk(clk), .clr(reset));
  Register #(.width(32)) register_28 (.D(WD3), .en(demultiplexer_1_out27), .Q(_27), .clk(clk), .clr(reset));
  Register #(.width(32)) register_29 (.D(WD3), .en(demultiplexer_1_out28), .Q(_28), .clk(clk), .clr(reset));
  Register #(.width(32)) register_30 (.D(WD3), .en(demultiplexer_1_out29), .Q(_29), .clk(clk), .clr(reset));
  Register #(.width(32)) register_31 (.D(WD3), .en(demultiplexer_1_out30), .Q(_30), .clk(clk), .clr(reset));
  Register #(.width(32)) register_32 (.D(WD3), .en(demultiplexer_1_out31), .Q(_31), .clk(clk), .clr(reset));
  Multiplexer #(.select(5), .width(32), .disabled(0), .enable("false")) multiplexer_1 (
    .in0(_0), .in1(_1), .in2(_2), .in3(_3), .in4(_4), .in5(_5), .in6(_6), .in7(_7), .in8(_8), .in9(_9),
    .in10(_10), .in11(_11), .in12(_12), .in13(_13), .in14(_14), .in15(_15), .in16(_16), .in17(_17),
    .in18(_18), .in19(_19), .in20(_20), .in21(_21), .in22(_22), .in23(_23), .in24(_24), .in25(_25),
    .in26(_26), .in27(_27), .in28(_28), .in29(_29), .in30(_30), .in31(_31), .out(RD1), .sel(A1));
  Multiplexer #(.select(5), .width(32), .disabled(0), .enable("false")) multiplexer_2 (
    .in0(_0), .in1(_1), .in2(_2), .in3(_3), .in4(_4), .in5(_5), .in6(_6), .in7(_7), .in8(_8), .in9(_9),
    .in10(_10), .in11(_11), .in12(_12), .in13(_13), .in14(_14), .in15(_15), .in16(_16), .in17(_17),
    .in18(_18), .in19(_19), .in20(_20), .in21(_21), .in22(_22), .in23(_23), .in24(_24), .in25(_25),
    .in26(_26), .in27(_27), .in28(_28), .in29(_29), .in30(_30), .in31(_31), .out(RD2), .sel(A2));

  // Other names for the same wires on the sheet: clr = reset; RegWrite = WE3

  // Notes on the sheet:
  //   $zero
  //   $at
  //   $v0
  //   $v1
  //   $a0
  //   $a1
  //   $a2
  //   $a3
  //   $t0
  //   $t1
  //   $t2
  //   $t3
  //   $t4
  //   $t5
  //   $t6
  //   $t7
  //   $s0
  //   $s1
  //   $s2
  //   $s3
  //   $s4
  //   $s5
  //   $s6
  //   $s7
  //   $t8
  //   $t9
  //   $k0
  //   $k1
  //   $gp
  //   $sp
  //   $fp
  //   $ra
endmodule

module CU (
  input  [5:0] opcode,
  input  [5:0] func,
  output out_3,
  output out_4,
  output out_5,
  output out_6,
  output out_7,
  output [1:0] out_8,
  output [1:0] out_9,
  output [2:0] out_10,
  output [3:0] out_11
);

  wire addi_out, beq_out, j_out, jal_out, lui_out, lw_out, not_1_out, not_2_out, not_3_out, not_4_out,
       not_5_out, not_6_out, NPCOp2, ori_out, R_instr_out, RegDataSrc1, sw_out;
  wire [2:0] ALUOp0_out;

  not not_1 (not_1_out, opcode[5]);
  not not_2 (not_2_out, opcode[4]);
  not not_3 (not_3_out, opcode[3]);
  not not_4 (not_4_out, opcode[1]);
  not not_5 (not_5_out, opcode[2]);
  not not_6 (not_6_out, opcode[0]);
  and R_instr (R_instr_out, not_1_out, not_2_out, not_3_out, not_5_out, not_4_out, not_6_out);
  and lw (lw_out, opcode[5], not_2_out, not_3_out, not_5_out, opcode[1], opcode[0]);
  and sw (sw_out, opcode[5], not_2_out, opcode[3], not_5_out, opcode[1], opcode[0]);
  and beq (beq_out, not_1_out, not_2_out, not_3_out, opcode[2], not_4_out, not_6_out);
  and addi (addi_out, not_1_out, not_2_out, opcode[3], not_5_out, not_4_out, not_6_out);
  and j (j_out, not_1_out, not_2_out, not_3_out, not_5_out, opcode[1], not_6_out);
  and ori (ori_out, not_1_out, not_2_out, opcode[3], opcode[2], not_4_out, opcode[0]);
  and lui (lui_out, not_1_out, not_2_out, opcode[3], opcode[2], opcode[1], opcode[0]);
  and jal (jal_out, not_1_out, not_2_out, not_3_out, not_5_out, opcode[1], opcode[0]);
  or u_RegDataSrc1 (out_9[1], jal_out, RegDataSrc1);
  buf RegDataSrc0 (out_9[0], lw_out);  // OR_Gate
  buf MemWrite (out_3, sw_out);  // OR_Gate
  buf u_NPCOp2 (out_10[2], NPCOp2);  // OR_Gate
  or NPCOp1 (out_10[1], j_out, jal_out);
  buf NPCOp0 (out_10[0], beq_out);  // OR_Gate
  or ExtOp (out_4, ori_out, lui_out);
  or ALUOp2 (ALUOp0_out[2], ori_out, lui_out);
  buf ALUOp1 (ALUOp0_out[1], R_instr_out);  // OR_Gate
  or ALUOp0 (ALUOp0_out[0], beq_out, lui_out);
  ALUDecoder aludecoder_1 (
    .func(func), .ALUControl(out_11), .ALUOp(ALUOp0_out), .NPC2(NPCOp2), .RegDataSrc1(RegDataSrc1));
  or ALUDataSrc (out_5, lw_out, sw_out, addi_out, ori_out, lui_out);
  or RegAddrSrc1 (out_8[1], jal_out, 1'b0);
  buf RegAddrSrc0 (out_8[0], R_instr_out);  // OR_Gate
  or RegWrite (out_6, jal_out, R_instr_out, lw_out, addi_out, ori_out, lui_out);
  buf MemDataSrc (out_7, 1'b0);  // OR_Gate
endmodule

module ALUDecoder (
  input  [5:0] func,
  input  [2:0] ALUOp,
  output [3:0] ALUControl,
  output NPC2,
  output RegDataSrc1
);

  wire add_2_out, add_out, addu_out, and_out, jalr_out, jr_out, lui_101_out, not_1_out, not_2_out, not_3_out,
       not_4_out, not_5_out, not_6_out, not_7_out, not_8_out, not_9_out, or_out, ori_100_out, sll_out,
       slt_out, sub_2_out, sub_out, subu_out;

  not not_1 (not_1_out, func[5]);
  not not_2 (not_2_out, func[4]);
  not not_3 (not_3_out, func[3]);
  not not_4 (not_4_out, func[1]);
  not not_5 (not_5_out, func[2]);
  not not_6 (not_6_out, func[0]);
  not not_7 (not_7_out, ALUOp[2]);
  not not_8 (not_8_out, ALUOp[1]);
  not not_9 (not_9_out, ALUOp[0]);
  and add (add_out, not_7_out, not_8_out, not_9_out);
  and sub (sub_out, not_7_out, not_8_out, ALUOp[0]);
  and add_2 (add_2_out, not_7_out, func[5], not_2_out, not_3_out, not_5_out, not_4_out, not_6_out, ALUOp[1]);
  and sub_2 (sub_2_out, not_7_out, func[5], not_2_out, not_3_out, not_5_out, func[1], not_6_out, ALUOp[1]);
  and \and  (and_out, not_7_out, func[5], not_2_out, not_3_out, func[2], not_4_out, not_6_out, ALUOp[1]);
  and \or  (or_out, not_7_out, func[5], not_2_out, not_3_out, func[2], not_4_out, func[0], ALUOp[1]);
  and slt (slt_out, not_7_out, func[5], not_2_out, func[3], not_5_out, func[1], not_6_out, ALUOp[1]);
  and addu (addu_out, func[5], not_2_out, not_3_out, not_5_out, not_4_out, func[0], not_7_out, ALUOp[1]);
  and subu (subu_out, func[5], not_2_out, not_3_out, not_5_out, func[1], func[0], not_7_out, ALUOp[1]);
  and ori_100 (ori_100_out, ALUOp[2], not_8_out, not_9_out);
  and lui_101 (lui_101_out, ALUOp[2], not_8_out, ALUOp[0]);
  and jalr (jalr_out, not_1_out, not_2_out, func[3], not_5_out, not_4_out, func[0], not_7_out, ALUOp[1]);
  and jr (jr_out, not_1_out, not_2_out, func[3], not_5_out, not_4_out, not_6_out, not_7_out, ALUOp[1]);
  and sll (sll_out, not_1_out, not_2_out, not_3_out, not_5_out, not_4_out, not_6_out, not_7_out, ALUOp[1]);
  buf or_2 (ALUControl[3], lui_101_out);  // OR_Gate
  or or_3 (ALUControl[2], sub_out, sub_2_out, slt_out, subu_out);
  or or_4 (ALUControl[1], sll_out, add_out, sub_out, add_2_out, sub_2_out, slt_out, addu_out, subu_out, jalr_out, jr_out);
  or or_5 (ALUControl[0], or_out, slt_out, ori_100_out, sll_out);
  or or_6 (NPC2, jalr_out, jr_out);
  buf or_7 (RegDataSrc1, jalr_out);  // OR_Gate
endmodule

module ALU (
  input  [3:0] ALUControl,
  input  [31:0] A,
  input  [31:0] B,
  input  [4:0] in_4,
  output out_5,
  output [31:0] out_6
);

  wire SEQ, SGT, SLT, undriven, undriven_2, undriven_3, undriven_4, undriven_5, undriven_6;
  wire [31:0] A_B, A_B_t, A_B_t_t, A_B_t_t_t, A_nB, A_nB_t, B__16, B__shamt, not_1_out, not_2_out, SGT32,
       SLT32;

  assign not_1_out = ~B;  // NOT_Gate not_1, 32 bits wide
  assign not_2_out = ~B;  // NOT_Gate not_2, 32 bits wide
  assign A_B = A & B;  // AND_Gate and_1, 32 bits wide
  assign A_nB = A & not_1_out;  // AND_Gate and_2, 32 bits wide
  assign A_B_t_t_t = A | B;  // OR_Gate or_1, 32 bits wide
  assign A_nB_t = A | not_2_out;  // OR_Gate or_2, 32 bits wide
  Adder #(.width(32)) adder_1 (.a(A), .b(B), .out(A_B_t));  // open: cin, cout
  Subtractor #(.width(32)) subtractor_1 (.a(A), .b(B), .out(A_B_t_t));  // open: bin, bout
  Comparator #(.width(32)) comparator_1 (.a(A), .b(B), .gt(SGT), .eq(SEQ), .lt(SLT));
  Shifter #(.width(32)) shifter_1 (.in(B), .\dist (5'b10000), .out(B__16));
  Shifter #(.width(32)) shifter_2 (.in(B), .\dist (in_4), .out(B__shamt));
  assign SGT32 = {{31{1'b0}}, SGT};  // Bit_Extender bit_extender_1
  assign SLT32 = {{31{1'b0}}, SLT};  // Bit_Extender bit_extender_2
  Multiplexer #(.select(4), .enable("false")) multiplexer_1 (
    .in0(undriven_4), .in1(undriven_5), .in2(undriven_6), .in3(undriven_2), .in4(undriven_3), .in5(undriven),
    .in6(SEQ), .in7(SLT), .out(out_5), .sel(ALUControl));  // open: in8, in9, in10, in11, in12, in13, in14, in15
  Multiplexer #(.select(4), .width(32), .enable("false")) multiplexer_2 (
    .in0(A_B), .in1(A_B_t_t_t), .in2(A_B_t), .in3(B__shamt), .in4(A_nB), .in5(A_nB_t), .in6(A_B_t_t),
    .in7(SLT32), .in8(B__16), .out(out_6), .sel(ALUControl));  // open: in9, in10, in11, in12, in13, in14, in15

  // Other names for the same wires on the sheet: shamt[4:0] = in_4

  // Notes on the sheet:
  //   B: pull=up
endmodule

module EXT (
  input  EXTOp,
  input  [15:0] in_2,
  output [31:0] out_3
);

  wire [31:0] bit_extender_1_out, bit_extender_2_out;

  assign bit_extender_1_out = {{16{in_2[15]}}, in_2};  // Bit_Extender bit_extender_1
  assign bit_extender_2_out = {{16{1'b0}}, in_2};  // Bit_Extender bit_extender_2
  Multiplexer #(.width(32), .enable("false")) multiplexer_1 (
    .in0(bit_extender_1_out), .in1(bit_extender_2_out), .out(out_3), .sel(EXTOp));
endmodule

module DM (
  input  in_1,
  input  in_2,
  input  [31:0] A,
  input  [31:0] WD,
  input  in_5,
  output [31:0] out_6
);

  RAM #(.addrWidth(10), .dataWidth(32), .bus("separate")) ram_1 (
    .addr(A[11:2]), .din(WD), .data(out_6), .str(in_2), .clk(in_1), .clr(in_5));  // open: sel, ld

  // Other names for the same wires on the sheet: clk = in_1; reset = in_5; WE = in_2
endmodule
