// Logisim project p3L0cpu.circ as structural Verilog: 8 circuits, main circuit main
module main (
  input  reset,
  output [31:0] out_2,
  output out_3,
  output [4:0] out_4,
  output [31:0] out_5,
  output out_6,
  output [4:0] out_7,
  output [31:0] out_8
);

  wire ALUSrc, beq, clk, eq, j_jal, jal, jr, RegDst, SignExt, WE_DM, WE_GRF, WeDM;
  wire [1:0] whichToRegister;
  wire [2:0] ALUOp;
  wire [4:0] multiplexer_1_out;
  wire [31:0] imm32, MemRead, multiplexer_3_out, multiplexer_5_out, PC_4, RegRead1, result;

  IFU ifu_1 (
    .imm32(imm32), .PC_jr(RegRead1), .PC_4(PC_4), .instr(out_2), .clk(clk), .beq(beq), .j_jal(j_jal),
    .reset(reset), .eq(eq), .jr(jr));
  Multiplexer #(.width(5), .enable("false")) multiplexer_1 (
    .in0(out_2[15:11]), .in1(out_2[20:16]), .out(multiplexer_1_out), .sel(RegDst));
  Multiplexer #(.width(5), .enable("false")) multiplexer_2 (
    .in0(multiplexer_1_out), .in1({5{1'b1}}), .out(out_4), .sel(jal));
  Multiplexer #(.select(2), .width(32), .enable("false")) multiplexer_3 (
    .in0({result[31:7], out_7, result[1:0]}), .in1(MemRead), .in2({out_2[15:0], {16{1'b0}}}),
    .out(multiplexer_3_out), .sel(whichToRegister));  // open: in3
  // Probe on whichToRegister
  EXT EXT (.imm16(out_2[15:0]), .sign(SignExt), .imm32(imm32));
  Multiplexer #(.width(32), .enable("false")) multiplexer_4 (
    .in0(multiplexer_3_out), .in1(PC_4), .out(out_5), .sel(jal));
  GRF GRF (
    .A1(out_2[25:21]), .A2(out_2[20:16]), .A3(out_4), .WD(out_5), .RD1(RegRead1), .RD2(out_8), .WE(WE_GRF),
    .clk(clk), .reset(reset));
  controller controller (
    .op(out_2[31:26]), .func(out_2[5:0]), .WE_GRF(WE_GRF), .SignExt(SignExt), .jal(jal), .WE_DM(WE_DM),
    .jr(jr), .beq(beq), .j_jal(j_jal), .ALUSrc(ALUSrc), .whichToRegister(whichToRegister), .RegDst(RegDst),
    .ALUOp(ALUOp));
  Clock clock_1 (.out(clk));
  Multiplexer #(.width(32), .enable("false")) multiplexer_5 (
    .in0(out_8), .in1(imm32), .out(multiplexer_5_out), .sel(ALUSrc));
  ALU ALU (
    .A(RegRead1), .B(multiplexer_5_out), .ALUresult({result[31:7], out_7, result[1:0]}), .equal(eq),
    .ALUOp(ALUOp));
  DM DM (.A(out_7), .WD(out_8), .RD(MemRead), .WE(WeDM), .clk(clk), .reset(reset));

  // Other names for the same wires on the sheet: func[5:0] = out_2[5:0]; imm16[15:0] = out_2[15:0];
  //   instr[31:0] = out_2; shamt[4:0] = out_2[10:6]; Rd[4:0] = out_2[15:11]; Rt[4:0] = out_2[20:16];
  //   Rs[4:0] = out_2[25:21]; op[5:0] = out_2[31:26]; MemWrite = out_6; RegAddr[4:0] = out_4; RegData[31:0] = out_5;
  //   Mem[31:0] = out_8; MemData[31:0] = out_8; RegRead2[31:0] = out_8; RegWrite = out_3; MemAddr[4:0] = out_7;
  //   result[6:2] = out_7

  // Notes on the sheet:
  //   연산자 3개
  //   연산자 2개
  //   연산자 없음
  //   addu, subu, ori, lw, sw, beq, lui, nop
  //   I타입: op6, rs5, rt5, imm16
  //   J타입: op6, address26
  //   MAIN
  //   CPU의 기능은 명령 실행을 제어하고, 프로세스는 가져오고, 실행하는 것이다(작업 메모리로부터).
  //   R타입: op6, rs5, rt5, rd5, shamt5, funct6
  //   실행 과정: fetch->명령어 세트에서 해당 명령어의 RTL 언어 찾기-> fetch -> 연산 -> (메모리 접근 연산) -> (레지스터에 값 쓰기) -> 다음 PC값 계산
  //   funct와 함께 명령어 종류 나타냄
  //   shift amount: shift양을 나타냄, 다른 명령어에서는 항상 0
  //   첫번째 피연산자 값이 들어있는 레지스터의 주소를 담고 있는 부분
  //   Rd = Rs, Rt /  값 연산하여 얻은 결과를 저장하는 레지스터의 주소를 담고 있는 부분
  //   두번째 피연산자 값이 들어있는 레지스터의 주소를 담고 있는 부분
  //   GRF 쓰기 제어 신호
  //   GRF 5비트 쓰기 주소
  //   GRF 32비트 쓰기 데이터
  //   DM 쓰기 제어 신호
  //   DM 5비트 쓰기 주소
  //   DM 32비트 쓰기 데이터
  //   32비트 명령 신호
endmodule

module controller (
  input  [5:0] op,
  input  [5:0] func,
  output WE_GRF,
  output SignExt,
  output jal,
  output WE_DM,
  output jr,
  output beq,
  output j_jal,
  output ALUSrc,
  output [1:0] whichToRegister,
  output RegDst,
  output [2:0] ALUOp
);

  wire addu, j, lui, lw, not_1_out, not_2_out, not_3_out, not_4_out, not_5_out, not_6_out, not_7_out,
       not_9_out, not_10_out, not_11_out, not_12_out, not_13_out, ori, R, subu;

  not not_1 (not_1_out, op[5]);
  not not_2 (not_2_out, op[4]);
  not not_3 (not_3_out, op[3]);
  or or_1 (ALUOp[0], subu, ori, 1'b0, 1'b0);
  buf or_2 (ALUOp[1], ori);  // OR_Gate
  buf or_3 (ALUOp[2], 1'b0);  // OR_Gate
  not not_4 (not_4_out, op[2]);
  not not_5 (not_5_out, op[1]);
  not not_6 (not_6_out, op[0]);
  or or_4 (whichToRegister[0], jal, lw);
  or or_5 (whichToRegister[1], jal, lui);
  not not_7 (not_7_out, func[5]);
  or or_6 (WE_GRF, addu, subu, lw, ori, lui, jal);
  or or_7 (ALUSrc, ori, lw, WE_DM, 1'b0);
  not not_8 (RegDst, R);
  not not_9 (not_9_out, func[3]);
  not not_10 (not_10_out, func[4]);
  not not_11 (not_11_out, func[1]);
  not not_12 (not_12_out, func[2]);
  not not_13 (not_13_out, func[0]);
  or or_8 (SignExt, lw, WE_DM, beq);
  or or_9 (j_jal, j, jal);
  and R_type (R, not_6_out, not_5_out, not_4_out, not_3_out, not_2_out, not_1_out);
  and u_addu (addu, R, func[0], not_11_out, not_12_out, not_9_out, not_10_out, func[5]);
  and u_subu (subu, R, func[0], func[1], not_12_out, not_9_out, not_10_out, func[5]);
  and u_ori (ori, op[0], not_5_out, op[2], op[3], not_2_out, not_1_out);
  and u_lw (lw, op[0], op[1], not_4_out, not_3_out, not_2_out, op[5]);
  and sw (WE_DM, op[0], op[1], not_4_out, op[4], not_2_out, op[5]);
  and u_beq (beq, not_6_out, not_5_out, op[3], not_3_out, not_2_out, not_1_out);
  and u_lui (lui, op[0], op[1], op[3], op[4], not_2_out, not_1_out);
  and u_j (j, not_6_out, op[1], not_4_out, not_3_out, not_2_out, not_1_out);
  and u_jal (jal, op[0], op[1], not_4_out, not_3_out, not_2_out, not_1_out);
  and u_jr (jr, R, not_13_out, not_11_out, not_12_out, func[3], not_10_out, not_7_out);

  // Other names for the same wires on the sheet: sw = WE_DM

  // Notes on the sheet:
  //   Controller
  //   not게이트랑 연결된게 0, 바로 가는게 1
  //   opcode줄에 있는건 op랑 연결, funct줄에 있는건 func이랑 연결
  //   기능 추가는 mips green sheet 보고 해당하는 binary 값읽어서 거꾸로 넣으면 됨
  //   여기서 나누는 기준은 R타입 / load or store / branch
  //   R타입은 rd가 목적지 레지스터이기 때문에 RegDst=1이다. 레지스터에 써야하기 때문에 RegWrite=1
  //   opcode가 전부 0 이면, R type
  //   만약 R type이라면, 7bit로 해서  R을 맨처음에 연결시켜줘야함
endmodule

module GRF (
  input  WE,
  input  clk,
  input  reset,
  input  [4:0] A1,
  input  [4:0] A2,
  input  [4:0] A3,
  input  [31:0] WD,
  output [31:0] RD1,
  output [31:0] RD2
);

  wire [31:0] _0_out, _1_in, _1_out, _2_in, _2_out, _3_in, _3_out, _4_in, _4_out, _5_in, _5_out, _6_in,
       _6_out, _7_in, _7_out, _8_in, _8_out, _9_in, _9_out, _10_in, _10_out, _11_in, _11_out, _12_in,
       _12_out, _13_in, _13_out, _14_in, _14_out, _15_in, _15_out, _16_in, _16_out, _17_in, _17_out, _18_in,
       _18_out, _19_in, _19_out, _20_in, _20_out, _21_in, _21_out, _22_in, _22_out, _23_in, _23_out, _24_in,
       _24_out, _25_in, _25_out, _26_in, _26_out, _27_in, _27_out, _28_in, _28_out, _29_in, _29_out, _30_in,
       _30_out, _31_in, _31_out;

  Register #(.width(32)) _0 (.D({32{1'b0}}), .en(WE), .Q(_0_out), .clk(clk), .clr(reset));
  Register #(.width(32)) _8 (.D(_8_in), .en(WE), .Q(_8_out), .clk(clk), .clr(reset));
  Register #(.width(32)) _16 (.D(_16_in), .en(WE), .Q(_16_out), .clk(clk), .clr(reset));
  Register #(.width(32)) _24 (.D(_24_in), .en(WE), .Q(_24_out), .clk(clk), .clr(reset));
  Multiplexer #(.select(5), .width(32)) multiplexer_1 (
    .in0(_0_out), .in1(_1_out), .in2(_2_out), .in3(_3_out), .in4(_4_out), .in5(_5_out), .in6(_6_out),
    .in7(_7_out), .in8(_8_out), .in9(_9_out), .in10(_10_out), .in11(_11_out), .in12(_12_out), .in13(_13_out),
    .in14(_14_out), .in15(_15_out), .in16(_16_out), .in17(_17_out), .in18(_18_out), .in19(_19_out),
    .in20(_20_out), .in21(_21_out), .in22(_22_out), .in23(_23_out), .in24(_24_out), .in25(_25_out),
    .in26(_26_out), .in27(_27_out), .in28(_28_out), .in29(_29_out), .in30(_30_out), .in31(_31_out),
    .out(RD1), .sel(A1));  // open: en
  Register #(.width(32)) _1 (.D(_1_in), .en(WE), .Q(_1_out), .clk(clk), .clr(reset));
  Register #(.width(32)) _9 (.D(_9_in), .en(WE), .Q(_9_out), .clk(clk), .clr(reset));
  Register #(.width(32)) _17 (.D(_17_in), .en(WE), .Q(_17_out), .clk(clk), .clr(reset));
  Register #(.width(32)) _25 (.D(_25_in), .en(WE), .Q(_25_out), .clk(clk), .clr(reset));
  Register #(.width(32)) _2 (.D(_2_in), .en(WE), .Q(_2_out), .clk(clk), .clr(reset));
  Register #(.width(32)) _10 (.D(_10_in), .en(WE), .Q(_10_out), .clk(clk), .clr(reset));
  Register #(.width(32)) _18 (.D(_18_in), .en(WE), .Q(_18_out), .clk(clk), .clr(reset));
  Register #(.width(32)) _26 (.D(_26_in), .en(WE), .Q(_26_out), .clk(clk), .clr(reset));
  Multiplexer #(.select(5), .width(32)) multiplexer_2 (
    .in0(_0_out), .in1(_1_out), .in2(_2_out), .in3(_3_out), .in4(_4_out), .in5(_5_out), .in6(_6_out),
    .in7(_7_out), .in8(_8_out), .in9(_9_out), .in10(_10_out), .in11(_11_out), .in12(_12_out), .in13(_13_out),
    .in14(_14_out), .in15(_15_out), .in16(_16_out), .in17(_17_out), .in18(_18_out), .in19(_19_out),
    .in20(_20_out), .in21(_21_out), .in22(_22_out), .in23(_23_out), .in24(_24_out), .in25(_25_out),
    .in26(_26_out), .in27(_27_out), .in28(_28_out), .in29(_29_out), .in30(_30_out), .in31(_31_out),
    .out(RD2), .sel(A2));  // open: en
  Register #(.width(32)) _3 (.D(_3_in), .en(WE), .Q(_3_out), .clk(clk), .clr(reset));
  Register #(.width(32)) _11 (.D(_11_in), .en(WE), .Q(_11_out), .clk(clk), .clr(reset));
  Register #(.width(32)) _19 (.D(_19_in), .en(WE), .Q(_19_out), .clk(clk), .clr(reset));
  Register #(.width(32)) _27 (.D(_27_in), .en(WE), .Q(_27_out), .clk(clk), .clr(reset));
  Demultiplexer #(.select(5), .width(32), .tristate("true")) demultiplexer_1 (
    .out1(_1_in), .out2(_2_in), .out3(_3_in), .out4(_4_in), .out5(_5_in), .out6(_6_in), .out7(_7_in),
    .out8(_8_in), .out9(_9_in), .out10(_10_in), .out11(_11_in), .out12(_12_in), .out13(_13_in),
    .out14(_14_in), .out15(_15_in), .out16(_16_in), .out17(_17_in), .out18(_18_in), .out19(_19_in),
    .out20(_20_in), .out21(_21_in), .out22(_22_in), .out23(_23_in), .out24(_24_in), .out25(_25_in),
    .out26(_26_in), .out27(_27_in), .out28(_28_in), .out29(_29_in), .out30(_30_in), .out31(_31_in), .in(WD),
    .sel(A3));  // open: out0, en
  Register #(.width(32)) _4 (.D(_4_in), .en(WE), .Q(_4_out), .clk(clk), .clr(reset));
  Register #(.width(32)) _12 (.D(_12_in), .en(WE), .Q(_12_out), .clk(clk), .clr(reset));
  Register #(.width(32)) _20 (.D(_20_in), .en(WE), .Q(_20_out), .clk(clk), .clr(reset));
  Register #(.width(32)) _28 (.D(_28_in), .en(WE), .Q(_28_out), .clk(clk), .clr(reset));
  Register #(.width(32)) _5 (.D(_5_in), .en(WE), .Q(_5_out), .clk(clk), .clr(reset));
  Register #(.width(32)) _13 (.D(_13_in), .en(WE), .Q(_13_out), .clk(clk), .clr(reset));
  Register #(.width(32)) _21 (.D(_21_in), .en(WE), .Q(_21_out), .clk(clk), .clr(reset));
  Register #(.width(32)) _29 (.D(_29_in), .en(WE), .Q(_29_out), .clk(clk), .clr(reset));
  Register #(.width(32)) _6 (.D(_6_in), .en(WE), .Q(_6_out), .clk(clk), .clr(reset));
  Register #(.width(32)) _14 (.D(_14_in), .en(WE), .Q(_14_out), .clk(clk), .clr(reset));
  Register #(.width(32)) _22 (.D(_22_in), .en(WE), .Q(_22_out), .clk(clk), .clr(reset));
  Register #(.width(32)) _30 (.D(_30_in), .en(WE), .Q(_30_out), .clk(clk), .clr(reset));
  Register #(.width(32)) _7 (.D(_7_in), .en(WE), .Q(_7_out), .clk(clk), .clr(reset));
  Register #(.width(32)) _15 (.D(_15_in), .en(WE), .Q(_15_out), .clk(clk), .clr(reset));
  Register #(.width(32)) _23 (.D(_23_in), .en(WE), .Q(_23_out), .clk(clk), .clr(reset));
  Register #(.width(32)) _31 (.D(_31_in), .en(WE), .Q(_31_out), .clk(clk), .clr(reset));

  // Notes on the sheet:
  //   * ReadData 읽기 부분
  //   GRF (Global Register File 전역 레지스터 파일)
  //   5비트 선택 신호와 32의 데이터 비트 폭을 가진 멀티플렉서를 사용하고 레지스터 출력 포트를 멀티플렉서의 입력에 연결하고 선택신호를 A1또는 A2출력 연결에 연결한다.
  //   * WriteData 쓰기 부분
  //   WD는 DMX 입력포트에 연결되고, 출력포트는 코드에 해당하는 레지스터에 연결되며 선택신호는 A3
  //   **주의** DMX를 three-state로 설정!!! 그렇지 않으면 쓸 때 다른 불필요한 레지스터를 0으로 할당해버림
endmodule

module ALU (
  input  [2:0] ALUOp,
  input  [31:0] A,
  input  [31:0] B,
  output [31:0] ALUresult,
  output equal
);

  wire [31:0] add, \and , \or , sub;

  Adder #(.width(32)) adder_1 (.a(A), .b(B), .out(add));  // open: cin, cout
  Subtractor #(.width(32)) subtractor_1 (.a(A), .b(B), .out(sub));  // open: bin, bout
  assign \and  = A & B;  // AND_Gate and_1, 32 bits wide
  assign \or  = A | B;  // OR_Gate or_1, 32 bits wide
  Multiplexer #(.select(3), .width(32), .enable("false")) multiplexer_1 (
    .in0(add), .in1(sub), .in2(\and ), .in3(\and ), .out(ALUresult), .sel(ALUOp));  // open: in4, in5, in6, in7
  Comparator #(.width(32)) comparator_1 (.a(B), .b(A), .eq(equal));  // open: gt, lt

  // Notes on the sheet:
  //   ALU (Arithmetic and Logic Unit 산술 논리 유닛)
endmodule

module IFU (
  input  clk,
  input  reset,
  input  [31:0] imm32,
  input  beq,
  input  eq,
  input  [31:0] PC_jr,
  input  j_jal,
  input  jr,
  output [31:0] PC_4,
  output [31:0] instr
);

  wire and_1_out;
  wire [1:0] PC_j_jal;
  wire [31:0] adder_1_out, multiplexer_1_out, multiplexer_2_out, NPC, PC, shifter_1_out;

  Shifter #(.width(32)) shifter_1 (.in(imm32), .\dist (5'b00010), .out(shifter_1_out));
  // Probe on shifter_1_out
  Register #(.width(32)) u_PC (.D(NPC), .Q(PC), .clk(clk), .clr(reset));  // open: en
  Adder #(.width(32)) adder_1 (.a(PC_4), .b(shifter_1_out), .out(adder_1_out));  // open: cin, cout
  and and_1 (and_1_out, beq, eq);
  // Probe on {PC[31:28], instr[25:0], PC_j_jal}
  Multiplexer #(.width(32), .enable("false")) multiplexer_1 (
    .in0(PC_4), .in1(adder_1_out), .out(multiplexer_1_out), .sel(and_1_out));
  Multiplexer #(.width(32), .enable("false")) multiplexer_2 (
    .in0(multiplexer_1_out), .in1({PC[31:28], instr[25:0], PC_j_jal}), .out(multiplexer_2_out), .sel(j_jal));
  ROM #(.addrWidth(5), .dataWidth(32)) rom_1 (.addr(PC[6:2]), .data(instr));  // open: sel
  Multiplexer #(.width(32), .enable("false")) multiplexer_3 (.in0(multiplexer_2_out), .in1(PC_jr), .out(NPC), .sel(jr));
  Adder #(.width(32)) adder_2 (.a(PC), .b(32'h4), .out(PC_4));  // open: cin, cout
  // Probe on PC_4

  // Other names for the same wires on the sheet: PC_j_jal[31:2] = {PC[31:28], instr[25:0]}

  // Notes on the sheet:
  //   2만큼 shift함
  //   IFU (Instruction Fetch Unit)
  //   명령어 가져오는 과정
  //   contents of rom_1 (hex, n*v repeats v):
  //   341c0000 341d0000 340080f8 36ee0367 3593769c 34dda539 3465c5dc 34be0ff1 3472af1d 35566602 35fe72a7
  //   3437ff23 37b9649e 3690bf9b 37fe4e0c 3711f49d 3c113bfe 3c057433 3c03c451 3c04c431 3c1c24d9 3c1bf0da
  //   3c0ccc68 3c0a118d 3c1021ea 3c0004d3 3c16115b 3c184f06 3c1215de 1000ffff
endmodule

module EXT (
  input  [15:0] imm16,
  input  sign,
  output [31:0] imm32
);

  wire [31:0] bit_extender_1_out, bit_extender_2_out;

  assign bit_extender_1_out = {{16{1'b0}}, imm16};  // Bit_Extender bit_extender_1
  assign bit_extender_2_out = {{16{imm16[15]}}, imm16};  // Bit_Extender bit_extender_2
  Multiplexer #(.width(32), .enable("false")) multiplexer_1 (
    .in0(bit_extender_1_out), .in1(bit_extender_2_out), .out(imm32), .sel(sign));

  // Notes on the sheet:
  //   EXT (Extend)
endmodule

module DM (
  input  WE,
  input  clk,
  input  reset,
  input  [4:0] A,
  input  [31:0] WD,
  output [31:0] RD
);

  RAM #(.addrWidth(5), .dataWidth(32), .bus("separate")) ram_1 (
    .addr(A), .din(WD), .data(RD), .str(WE), .clk(clk), .clr(reset));  // open: sel, ld

  // Notes on the sheet:
  //   DM (Data Memory)
endmodule

module test (
  output [31:0] out_1,
  output out_2,
  output [4:0] out_3,
  output out_4,
  output [31:0] out_5,
  output halt,
  output [4:0] out_7,
  output [31:0] out_8
);

  wire clock_1_out, comparator_1_gt;
  wire [7:0] counter_1_q;

  Counter counter_1 (.Q(counter_1_q), .carry(halt), .clk(clock_1_out));  // open: load, D, count, clr
  Clock clock_1 (.out(clock_1_out));
  Comparator comparator_1 (.a(8'h4), .b(counter_1_q), .gt(comparator_1_gt));  // open: eq, lt
  main main_1 (
    .reset(comparator_1_gt), .out_2(out_1), .out_3(out_2), .out_4(out_3), .out_5(out_5), .out_6(out_4),
    .out_7(out_7), .out_8(out_8));
endmodule
