// Logisim project p3cpu.circ as structural Verilog: 11 circuits, main circuit main
module main (
  input  reset,
  output [31:0] out_2,
  output out_3,
  output [4:0] out_4,
  output [31:0] out_5,
  output out_6,
  output [4:0] out_7,
  output [31:0] out_8
);

  wire aluSrc, branch, clk, extOp, jump, MemRead, RegDst, zero;
  wire [1:0] memToReg;
  wire [2:0] aluCtrl;
  wire [4:0] splitter_1_rd, splitter_1_rs, splitter_1_rt;
  wire [5:0] splitter_1_funccode, splitter_1_opcode;
  wire [31:0] alu_1_result, dm_1_rd, ext_1_out, grf_1_rd1, imm32, multiplexer_2_out;
  wire [31:16] splitter_1_imm16;

  IFU ifu_1 (.reset(reset), .clk(clk), .imm32(imm32), .zero(zero), .branch(branch), .instr(out_2));
  splitter splitter_1 (
    .in_1(out_2), .funccode(splitter_1_funccode), .rd(splitter_1_rd), .rt(splitter_1_rt), .rs(splitter_1_rs),
    .opcode(splitter_1_opcode), .imm16(splitter_1_imm16));  // open: add26
  Multiplexer #(.width(5), .enable("false")) multiplexer_1 (
    .in0(splitter_1_rt), .in1(splitter_1_rd), .out(out_4), .sel(RegDst));
  controller controller_1 (
    .op(splitter_1_opcode), .func(splitter_1_funccode), .RegDst(RegDst), .aluSrc(aluSrc), .regWrite(out_3),
    .memRead(MemRead), .memWrite(out_6), .memToReg(memToReg), .extOp(extOp), .branch(branch),
    .aluCtrl(aluCtrl), .jump(jump));
  GRF grf_1 (
    .ra1(splitter_1_rs), .ra2(splitter_1_rt), .wa(out_4), .RD1(grf_1_rd1), .RD2(out_8), .WE(out_3),
    .clk(clk), .reset(reset));  // open: wd
  ext ext_1 (.in(splitter_1_imm16), .out(ext_1_out), .extOp(extOp));
  Multiplexer #(.width(32), .enable("false")) multiplexer_2 (
    .in0(out_8), .in1(ext_1_out), .out(multiplexer_2_out), .sel(aluSrc));
  alu alu_1 (
    .A(grf_1_rd1), .B(multiplexer_2_out), .ALUOp(aluCtrl),
    .result({alu_1_result[31:7], out_7, alu_1_result[1:0]}), .zero(zero));
  DM dm_1 (
    .a({alu_1_result[31:7], out_7, alu_1_result[1:0]}), .wd(out_8), .rd(dm_1_rd), .MemWrite(out_6),
    .clk(clk), .MemRead(MemRead), .reset(reset));
  Multiplexer #(.select(2), .width(32), .enable("false")) multiplexer_3 (
    .in0({alu_1_result[31:7], out_7, alu_1_result[1:0]}), .in1({splitter_1_imm16, {16{1'b0}}}),
    .in2(dm_1_rd), .out(out_5), .sel(memToReg));  // open: in3
  Clock u_clk (.out(clk));

  // Other names for the same wires on the sheet: MemAddr[4:0] = out_7; instr[31:0] = out_2; MemData[31:0] = out_8;
  //   MemWrite = out_6; RegAddr[4:0] = out_4; RegData[31:0] = out_5; RegWrite = out_3

  // Notes on the sheet:
  //   연산자 3개
  //   연산자 2개
  //   연산자 없음
  //   addu, subu, ori, lw, sw, beq, lui, nop
  //   I타입: op6, rs5, rt5, imm16
  //   J타입: op6, address26
  //   MAIN
  //   CPU의 기능은 명령 실행을 제어하고, 프로세스는 가져오고, 실행하는 것이다(작업 메모리로부터).
  //   R타입: op6, rs5, rt5, rd5, shamt5, funct6
  //   실행 과정: fetch->명령어 세트에서 해당 명령어의 RTL 언어 찾기-> fetch -> 연산 -> (메모리 접근 연산) -> (레지스터에 값 쓰기) -> 다음 PC값 계산
  //   GRF 쓰기 제어 신호
  //   GRF 5비트 쓰기 주소
  //   GRF 32비트 쓰기 데이터
  //   DM 쓰기 제어 신호
  //   DM 5비트 쓰기 주소
  //   DM 32비트 쓰기 데이터
  //   32비트 명령 신호
endmodule

module IFU (
  input  reset,
  input  clk,
  input  [31:0] imm32,
  input  zero,
  input  branch,
  output [31:0] instr
);

  wire and_1_out, comparator_1_eq;
  wire [31:0] adder_1_out, adder_2_out, multiplexer_1_out, npc, pc, PC_2_q, PC_q, shifter_1_out;

  Adder #(.width(32)) adder_1 (.a(PC_2_q), .b(32'h4), .out(adder_1_out));  // open: cin, cout
  Shifter #(.width(32)) shifter_1 (.in(imm32), .\dist (5'b00010), .out(shifter_1_out));
  Register #(.width(32)) u_PC (.D(npc), .Q(PC_q), .clk(clk), .clr(reset));  // open: en
  Adder #(.width(32)) adder_2 (.a(adder_1_out), .b(shifter_1_out), .out(adder_2_out));  // open: cin, cout
  and and_1 (and_1_out, zero, branch);
  Comparator #(.width(32)) comparator_1 (.a({32{1'b0}}), .b(PC_q), .eq(comparator_1_eq));  // open: gt, lt
  Multiplexer #(.width(32), .enable("false")) multiplexer_1 (
    .in0(adder_1_out), .in1(adder_2_out), .out(multiplexer_1_out), .sel(and_1_out));
  Register #(.width(32)) PC_2 (.D(multiplexer_1_out), .Q(PC_2_q), .clk(clk), .clr(reset));  // open: en
  Multiplexer #(.width(32), .enable("false")) multiplexer_2 (
    .in0(PC_q), .in1(32'h3000), .out(pc), .sel(comparator_1_eq));
  Multiplexer #(.width(32), .enable("false")) multiplexer_3 (.in0(npc), .in1(32'h3000), .out(pc), .sel(reset));
  IM IM (.addr(PC_2_q[6:2]), .instr(instr));

  // Other names for the same wires on the sheet: imm[31:0] = imm32

  // Notes on the sheet:
  //   비동기식 리셋: 클록 펄스 관계없이 리셋 신호에 의해서만 리셋;  0x000030000으로 reset
  //   동기식 리셋: 클록 펄스의 상승/하강 엣지에 맞춰 리셋 신호에 의해 리셋
endmodule

module IM (
  input  [4:0] addr,
  output [31:0] instr
);

  ROM #(.addrWidth(5), .dataWidth(32)) rom_1 (.addr(addr), .data(instr));  // open: sel

  // Notes on the sheet:
  //   contents of rom_1 (hex, n*v repeats v):
  //   341c0000 341d0000 340080f8 36ee0367 3593769c 34dda539 3465c5dc 34be0ff1 3472af1d 35566602 35fe72a7
  //   3437ff23 37b9649e 3690bf9b 37fe4e0c 3711f49d 3c113bfe 3c057433 3c03c451 3c04c431 3c1c24d9 3c1bf0da
  //   3c0ccc68 3c0a118d 3c1021ea 3c0004d3 3c16115b 3c184f06 3c1215de 1000ffff
endmodule

module GRF (
  input  WE,
  input  clk,
  input  reset,
  input  [4:0] ra1,
  input  [4:0] ra2,
  input  [4:0] wa,
  input  [31:0] wd,
  output [31:0] RD1,
  output [31:0] RD2
);

  wire [31:0] _0_out, _1_in, _1_out, _2_in, _2_out, _3_in, _3_out, _4_in, _4_out, _5_in, _5_out, _6_in,
       _6_out, _7_in, _7_out, _8_in, _8_out, _9_in, _9_out, _10_in, _10_out, _11_in, _11_out, _12_in,
       _12_out, _13_in, _13_out, _14_in, _14_out, _15_in, _15_out, _16_in, _16_out, _17_in, _17_out, _18_in,
       _18_out, _19_in, _19_out, _20_in, _20_out, _21_in, _21_out, _22_in, _22_out, _23_in, _23_out, _24_in,
       _24_out, _25_in, _25_out, _26_in, _26_out, _27_in, _27_out, _28_in, _28_out, _29_in, _29_out, _30_in,
       _30_out, _31_in, _31_out;

  Register #(.width(32)) _0 (.D({32{1'b0}}), .en(WE), .Q(_0_out), .clk(clk), .clr(reset));
  Register #(.width(32)) _8 (.D(_8_in), .en(WE), .Q(_8_out), .clk(clk), .clr(reset));
  Register #(.width(32)) _16 (.D(_16_in), .en(WE), .Q(_16_out), .clk(clk), .clr(reset));
  Register #(.width(32)) _24 (.D(_24_in), .en(WE), .Q(_24_out), .clk(clk), .clr(reset));
  Multiplexer #(.select(5), .width(32)) multiplexer_1 (
    .in0(_0_out), .in1(_1_out), .in2(_2_out), .in3(_3_out), .in4(_4_out), .in5(_5_out), .in6(_6_out),
    .in7(_7_out), .in8(_8_out), .in9(_9_out), .in10(_10_out), .in11(_11_out), .in12(_12_out), .in13(_13_out),
    .in14(_14_out), .in15(_15_out), .in16(_16_out), .in17(_17_out), .in18(_18_out), .in19(_19_out),
    .in20(_20_out), .in21(_21_out), .in22(_22_out), .in23(_23_out), .in24(_24_out), .in25(_25_out),
    .in26(_26_out), .in27(_27_out), .in28(_28_out), .in29(_29_out), .in30(_30_out), .in31(_31_out),
    .out(RD1), .sel(ra1));  // open: en
  Register #(.width(32)) _1 (.D(_1_in), .en(WE), .Q(_1_out), .clk(clk), .clr(reset));
  Register #(.width(32)) _9 (.D(_9_in), .en(WE), .Q(_9_out), .clk(clk), .clr(reset));
  Register #(.width(32)) _17 (.D(_17_in), .en(WE), .Q(_17_out), .clk(clk), .clr(reset));
  Register #(.width(32)) _25 (.D(_25_in), .en(WE), .Q(_25_out), .clk(clk), .clr(reset));
  Register #(.width(32)) _2 (.D(_2_in), .en(WE), .Q(_2_out), .clk(clk), .clr(reset));
  Register #(.width(32)) _10 (.D(_10_in), .en(WE), .Q(_10_out), .clk(clk), .clr(reset));
  Register #(.width(32)) _18 (.D(_18_in), .en(WE), .Q(_18_out), .clk(clk), .clr(reset));
  Register #(.width(32)) _26 (.D(_26_in), .en(WE), .Q(_26_out), .clk(clk), .clr(reset));
  Multiplexer #(.select(5), .width(32)) multiplexer_2 (
    .in0(_0_out), .in1(_1_out), .in2(_2_out), .in3(_3_out), .in4(_4_out), .in5(_5_out), .in6(_6_out),
    .in7(_7_out), .in8(_8_out), .in9(_9_out), .in10(_10_out), .in11(_11_out), .in12(_12_out), .in13(_13_out),
    .in14(_14_out), .in15(_15_out), .in16(_16_out), .in17(_17_out), .in18(_18_out), .in19(_19_out),
    .in20(_20_out), .in21(_21_out), .in22(_22_out), .in23(_23_out), .in24(_24_out), .in25(_25_out),
    .in26(_26_out), .in27(_27_out), .in28(_28_out), .in29(_29_out), .in30(_30_out), .in31(_31_out),
    .out(RD2), .sel(ra2));  // open: en
  Register #(.width(32)) _3 (.D(_3_in), .en(WE), .Q(_3_out), .clk(clk), .clr(reset));
  Register #(.width(32)) _11 (.D(_11_in), .en(WE), .Q(_11_out), .clk(clk), .clr(reset));
  Register #(.width(32)) _19 (.D(_19_in), .en(WE), .Q(_19_out), .clk(clk), .clr(reset));
  Register #(.width(32)) _27 (.D(_27_in), .en(WE), .Q(_27_out), .clk(clk), .clr(reset));
  Demultiplexer #(.select(5), .width(32), .tristate("true")) demultiplexer_1 (
    .out1(_1_in), .out2(_2_in), .out3(_3_in), .out4(_4_in), .out5(_5_in), .out6(_6_in), .out7(_7_in),
    .out8(_8_in), .out9(_9_in), .out10(_10_in), .out11(_11_in), .out12(_12_in), .out13(_13_in),
    .out14(_14_in), .out15(_15_in), .out16(_16_in), .out17(_17_in), .out18(_18_in), .out19(_19_in),
    .out20(_20_in), .out21(_21_in), .out22(_22_in), .out23(_23_in), .out24(_24_in), .out25(_25_in),
    .out26(_26_in), .out27(_27_in), .out28(_28_in), .out29(_29_in), .out30(_30_in), .out31(_31_in), .in(wd),
    .sel(wa));  // open: out0, en
  Register #(.width(32)) _4 (.D(_4_in), .en(WE), .Q(_4_out), .clk(clk), .clr(reset));
  Register #(.width(32)) _12 (.D(_12_in), .en(WE), .Q(_12_out), .clk(clk), .clr(reset));
  Register #(.width(32)) _20 (.D(_20_in), .en(WE), .Q(_20_out), .clk(clk), .clr(reset));
  Register #(.width(32)) _28 (.D(_28_in), .en(WE), .Q(_28_out), .clk(clk), .clr(reset));
  Register #(.width(32)) _5 (.D(_5_in), .en(WE), .Q(_5_out), .clk(clk), .clr(reset));
  Register #(.width(32)) _13 (.D(_13_in), .en(WE), .Q(_13_out), .clk(clk), .clr(reset));
  Register #(.width(32)) _21 (.D(_21_in), .en(WE), .Q(_21_out), .clk(clk), .clr(reset));
  Register #(.width(32)) _29 (.D(_29_in), .en(WE), .Q(_29_out), .clk(clk), .clr(reset));
  Register #(.width(32)) _6 (.D(_6_in), .en(WE), .Q(_6_out), .clk(clk), .clr(reset));
  Register #(.width(32)) _14 (.D(_14_in), .en(WE), .Q(_14_out), .clk(clk), .clr(reset));
  Register #(.width(32)) _22 (.D(_22_in), .en(WE), .Q(_22_out), .clk(clk), .clr(reset));
  Register #(.width(32)) _30 (.D(_30_in), .en(WE), .Q(_30_out), .clk(clk), .clr(reset));
  Register #(.width(32)) _7 (.D(_7_in), .en(WE), .Q(_7_out), .clk(clk), .clr(reset));
  Register #(.width(32)) _15 (.D(_15_in), .en(WE), .Q(_15_out), .clk(clk), .clr(reset));
  Register #(.width(32)) _23 (.D(_23_in), .en(WE), .Q(_23_out), .clk(clk), .clr(reset));
  Register #(.width(32)) _31 (.D(_31_in), .en(WE), .Q(_31_out), .clk(clk), .clr(reset));

  // Other names for the same wires on the sheet: A2[4:0] = ra2; A3[4:0] = wa

  // Notes on the sheet:
  //   * ReadData 읽기 부분
  //   GRF (Global Register File 전역 레지스터 파일)
  //   5비트 선택 신호와 32의 데이터 비트 폭을 가진 멀티플렉서를 사용하고 레지스터 출력 포트를 멀티플렉서의 입력에 연결하고 선택신호를 A1또는 A2출력 연결에 연결한다.
  //   * WriteData 쓰기 부분
  //   WD는 DMX 입력포트에 연결되고, 출력포트는 코드에 해당하는 레지스터에 연결되며 선택신호는 A3
  //   **주의** DMX를 three-state로 설정!!! 그렇지 않으면 쓸 때 다른 불필요한 레지스터를 0으로 할당해버림
endmodule

module controller (
  input  [5:0] op,
  input  [5:0] func,
  output RegDst,
  output aluSrc,
  output regWrite,
  output memRead,
  output memWrite,
  output [1:0] memToReg,
  output extOp,
  output branch,
  output [2:0] aluCtrl,
  output jump
);

  wire jal, jr, not_1_out, not_2_out, not_3_out, not_4_out, not_5_out, not_6_out, not_7_out, not_8_out,
       not_9_out, not_10_out, not_11_out, not_12_out;
  wire [1:0] or_4_out;

  not not_1 (not_1_out, op[5]);
  not not_2 (not_2_out, op[4]);
  not not_3 (not_3_out, op[3]);
  not not_4 (not_4_out, op[1]);
  not not_5 (not_5_out, op[2]);
  not not_6 (not_6_out, op[0]);
  not not_7 (not_7_out, func[5]);
  not not_8 (not_8_out, func[4]);
  not not_9 (not_9_out, func[3]);
  not not_10 (not_10_out, func[2]);
  not not_11 (not_11_out, func[1]);
  not not_12 (not_12_out, func[0]);
  and R_type (RegDst, not_6_out, not_4_out, not_5_out, not_3_out, not_2_out, not_1_out);
  and ori (extOp, op[0], not_4_out, op[2], op[3], not_2_out, not_1_out);
  and lw (memRead, op[0], op[1], not_5_out, not_3_out, not_2_out, op[5]);
  and sw (memWrite, op[0], op[1], not_5_out, op[4], not_2_out, op[5]);
  and beq (branch, not_6_out, not_4_out, op[3], not_3_out, not_2_out, not_1_out);
  and lui (memToReg[0], op[0], op[1], op[3], op[4], not_2_out, not_1_out);
  and j (jump, not_6_out, op[1], not_5_out, not_3_out, not_2_out, not_1_out);
  and u_jal (jal, op[0], op[1], not_5_out, not_3_out, not_2_out, not_1_out);
  and u_jr (jr, RegDst, not_12_out, not_11_out, not_10_out, func[3], not_8_out, not_7_out);
  or or_1 (aluSrc, memRead, memWrite, extOp);
  or or_2 (regWrite, RegDst, memRead, memToReg[0], extOp);
  or or_3 (or_4_out[1], branch, memToReg[0], extOp);
  or or_4 (or_4_out[0], memRead, memWrite, memToReg[0], extOp);
  aluCtrl u_aluCtrl (.aluOp({extOp, or_4_out}), .func(func), .aluCtrl(aluCtrl));

  assign memToReg[1] = memRead;

  // Other names for the same wires on the sheet: ori = extOp; beq = branch; j = jump; lui = memToReg[0]; lw = memRead;
  //   R = RegDst; sw = memWrite

  // Notes on the sheet:
  //   Controller
  //   not게이트랑 연결된게 0, 바로 가는게 1
  //   opcode줄에 있는건 op랑 연결, funct줄에 있는건 func이랑 연결
  //   기능 추가는 mips green sheet 보고 해당하는 binary 값읽어서 거꾸로 넣으면 됨
  //   여기서 나누는 기준은 R타입 / load or store / branch
  //   R타입은 rd가 목적지 레지스터이기 때문에 RegDst=1이다. 레지스터에 써야하기 때문에 RegWrite=1
  //   opcode가 전부 0 이면, R type
  //   만약 R type이라면, 7bit로 해서  R을 맨처음에 연결시켜줘야함
endmodule

module DM (
  input  [31:0] a,
  input  clk,
  input  reset,
  input  MemWrite,
  input  MemRead,
  input  [31:0] wd,
  output [31:0] rd
);

  RAM #(.addrWidth(5), .dataWidth(32), .bus("separate")) ram_1 (
    .addr(a[6:2]), .din(wd), .data(rd), .str(MemWrite), .clk(clk), .ld(MemRead), .clr(reset));  // open: sel

  // Notes on the sheet:
  //   데이터 주소 신호
  //   WE가 하이레벨일때, 주소 a의 데이터 write
endmodule

module alu (
  input  [2:0] ALUOp,
  input  [31:0] A,
  input  [31:0] B,
  output [31:0] result,
  output zero
);

  wire comparator_1_gt;
  wire [31:0] add, \and , bit_extender_1_out, \or , sub;

  Adder #(.width(32)) adder_1 (.a(A), .b(B), .out(add));  // open: cin, cout
  Subtractor #(.width(32)) subtractor_1 (.a(A), .b(B), .out(sub));  // open: bin, bout
  assign \and  = A & B;  // AND_Gate and_1, 32 bits wide
  assign \or  = A | B;  // OR_Gate or_1, 32 bits wide
  Comparator #(.width(32)) comparator_1 (.a(A), .b(B), .gt(comparator_1_gt), .eq(zero));  // open: lt
  assign bit_extender_1_out = {{31{1'b0}}, comparator_1_gt};  // Bit_Extender bit_extender_1
  Multiplexer #(.select(3), .width(32), .enable("false")) multiplexer_1 (
    .in0(\and ), .in1(\or ), .in2(add), .in3(sub), .in5(bit_extender_1_out), .out(result), .sel(ALUOp));  // open: in4, in6, in7

  // Other names for the same wires on the sheet: aluCtrl[2:0] = ALUOp

  // Notes on the sheet:
  //   ALU (Arithmetic and Logic Unit 산술 논리 유닛)
endmodule

module ext (
  input  [15:0] in,
  input  extOp,
  output [31:0] out
);

  wire [31:0] bit_extender_1_out, bit_extender_2_out;

  assign bit_extender_1_out = {{16{1'b0}}, in};  // Bit_Extender bit_extender_1
  assign bit_extender_2_out = {{16{1'b0}}, in};  // Bit_Extender bit_extender_2
  Multiplexer #(.width(32), .enable("false")) multiplexer_1 (
    .in0(bit_extender_1_out), .in1(bit_extender_2_out), .out(out), .sel(extOp));
endmodule

module aluCtrl (
  input  [2:0] aluOp,
  input  [5:0] func,
  output [2:0] aluCtrl
);

  wire addu_out, beq_out, not_1_out, not_2_out, not_3_out, not_4_out, not_5_out, not_6_out, not_7_out,
       not_8_out, not_9_out, ori_out, subu_out, sw_lw_out;

  not not_1 (not_1_out, aluOp[2]);
  not not_2 (not_2_out, aluOp[0]);
  not not_3 (not_3_out, aluOp[1]);
  not not_4 (not_4_out, func[5]);
  not not_5 (not_5_out, func[4]);
  not not_6 (not_6_out, func[3]);
  not not_7 (not_7_out, func[2]);
  not not_8 (not_8_out, func[1]);
  not not_9 (not_9_out, func[0]);
  and sw_lw (sw_lw_out, not_1_out, not_3_out, aluOp[0]);
  and beq (beq_out, not_1_out, aluOp[1], not_2_out);
  and lui_j (aluCtrl[2], not_1_out, aluOp[1], aluOp[0]);
  and ori (ori_out, aluOp[2], aluOp[1], aluOp[0]);
  and addu (addu_out, not_1_out, not_3_out, not_2_out, func[5], not_5_out, not_6_out, not_7_out, not_8_out, func[0]);
  and subu (subu_out, not_1_out, not_3_out, not_2_out, func[5], not_5_out, not_6_out, not_7_out, func[1], func[0]);
  or or_1 (aluCtrl[1], sw_lw_out, beq_out, aluCtrl[2], addu_out, subu_out);
  or or_2 (aluCtrl[0], beq_out, aluCtrl[2], subu_out, ori_out);
endmodule

module splitter (
  input  [31:0] in_1,
  output [5:0] funccode,
  output [4:0] rd,
  output [4:0] rt,
  output [4:0] rs,
  output [5:0] opcode,
  output [15:0] imm16,
  output [25:0] add26
);

  Bit_Extender #(.in_width(32)) bit_extender_1 (.in(in_1), .out(imm16));
  Bit_Extender #(.in_width(32), .out_width(26)) bit_extender_2 (.in(in_1), .out(add26));

  assign funccode = in_1[5:0];
  assign opcode = in_1[31:26];
  assign rd = in_1[15:11];
  assign rs = in_1[25:21];
  assign rt = in_1[20:16];
endmodule

module test (
  output [31:0] out_1,
  output out_2,
  output [4:0] out_3,
  output out_4,
  output [31:0] out_5,
  output [4:0] out_6,
  output halt,
  output [31:0] out_8
);

  wire clock_1_out, comparator_1_gt;
  wire [4:0] counter_1_q;

  Counter #(.width(5), .max('h1f), .ongoal("stay")) counter_1 (
    .Q(counter_1_q), .carry(halt), .clk(clock_1_out));  // open: load, D, count, clr
  Clock clock_1 (.out(clock_1_out));
  Comparator #(.width(5), .mode("unsigned")) comparator_1 (
    .a(5'b00100), .b(counter_1_q), .gt(comparator_1_gt));  // open: eq, lt
  main main_1 (
    .reset(comparator_1_gt), .out_2(out_1), .out_3(out_2), .out_4(out_3), .out_5(out_5), .out_6(out_4),
    .out_7(out_6), .out_8(out_8));
endmodule
